# Fritzing sketch spi threading (saved by Fritzing 0.9.4)
breadboards: 2

parts:
  U1 = ST7735 1.8 inch TFT LCD [package="SIP (Single Inline) [THT]"]
  Mod1 = Raspberry Pi Pico W
  LED1 = LED - 3mm [color="White (6500K)" package="3 mm [THT]"]
  LED2 = LED - 3mm [color="Infrared (880nm)" package="3 mm [THT]"]
  LED4 = LED - 3mm [color="Red (633nm)" package="3 mm [THT]"]
  LED5 = LED - 3mm [color="Green (560nm)" package="3 mm [THT]"]
  LED6 = LED - 3mm [color="Yellow (592nm)" package="3 mm [THT]"]
  S1 = Pushbutton [package="[THT]"]
  LED3 = LED - 3mm [color="Blue (525nm)" package="3 mm [THT]"]
  U2 = POT [package=pot_alpha_rv16af-20]

nets:
  N1: U1.RST, Mod1.pin_22
  N2: U1.A0, Mod1.pin_21
  N3: U1.SDA, Mod1.pin_10
  N4: U1.SCK, Mod1.pin_9
  N5: U1.VCC, Mod1.pin_36, S1.Pin_3, S1.Pin_4, U2.A
  N6: U1.CS, Mod1.pin_24
  N7: U1.GND, Mod1.pin_3, Mod1.pin_28, Mod1.pin_38, LED1.cathode, LED2.cathode, LED4.cathode, LED5.cathode, LED6.cathode, LED3.cathode, U2.E
  N8: Mod1.pin_2, LED2.anode
  N9: Mod1.pin_5, S1.Pin_1, S1.Pin_2
  N10: Mod1.pin_6, LED5.anode
  N11: Mod1.pin_7, LED1.anode
  N12: Mod1.pin_14, LED3.anode
  N13: Mod1.pin_31, U2.S
  N14: Mod1.pin_32, LED4.anode
  N15: Mod1.pin_34, LED6.anode

notes:
  Threading Demonstration

custom parts:
  ST7735 1.8 inch TFT LCD: 1.8 inch TFT LCD module. SPI interface, ST7735 controller
  Raspberry Pi Pico W: Raspberry Pi Pico W. Based around the RP2040 microcontroller the Pico W is a low cost microcontroller device bringing Raspberry Pi quality, cost, and easy of use to the microcontroller space. The areas marked KEEPOUT in pcb silkscreen should not have traces running through them to avoid shorts on a soldered in module!
